# Fritzing sketch scarf (saved by Fritzing 0.9.9b)

parts:
  Arduino = Arduino Pro Mini (3.3V)
  Charger = USB LiPoly Charger
  LiPoly_battery = LIPO-1000mAh [package=lipo-1000]
  Led_Strip = WS2812 RGB LED strip

nets:
  VCC: Arduino.VCC, Charger.VBAT, LiPoly_battery.+, Led_Strip.VCC
  GND: Arduino.GND, Charger.GND, LiPoly_battery.-, Led_Strip.GND
  N1: Arduino.D6, Led_Strip.DIN

custom parts:
  WS2812 RGB LED strip: WS2812 strip
